# Fritzing sketch circuit layout (saved by Fritzing 0.9.3b)
stripboards: 1

parts:
  R3 = Trimmer Potentiometer [maximum_resistance=10kΩ package=THT]
  R4 = Trimmer Potentiometer [maximum_resistance=10kΩ package=THT]
  Part1 = Arduino Nano (Rev3.0)
  U1 = mystery part, 4 pins [chip_label="Motor A"]
  U2 = mystery part, 4 pins [chip_label="Motor B"]
  Grove1 = Grove OLED 128x96
  R5 = Resistor [tolerance=±5% resistance=10k package=THT]
  R6 = Resistor [tolerance=±5% resistance=10k package=THT]

nets:
  VIN: R3.leg1, R4.leg1, Part1.VIN, U1.pin4, U2.pin4, Grove1.VCC, R5.Pin_0, R6.Pin_0
  N1: R3.wiper, Part1.A1
  GND: R3.leg2, R4.leg2, Part1.GND, U1.pin3, U2.pin3, Grove1.GND
  N2: R4.wiper, Part1.A2
  N3: Part1.D2, U1.pin2, R5.Pin_1
  N4: Part1.D3, U2.pin2, R6.Pin_1
  N5: Part1.D4, U1.pin1
  N6: Part1.D5, U2.pin1
  N7: Part1.A5, Grove1.SCL
  N8: Part1.A4, Grove1.SDA
